# Fritzing sketch smart_bottle (saved by Fritzing 0.9.3b)
breadboards: 1

parts:
  U1 = NodeMCU V1.0
  U2 = LCD-16X2 [package=lcd-16x2_noholes]
  R2 = Rotary Potentiometer (Large) [maximum_resistance=100kΩ package=THT]
  Part1 = Matrix LED de 8x8 basada en MAX7219

nets:
  N1: U1.D0, U2.RS
  N2: U1.D1, U2.E, U2.DB0
  N3: U1.D2, U2.DB4
  N4: U1.D3, U2.DB5
  N5: U1.D4, U2.DB6
  3V3: U1.3V3, U2.VDD, U2.A, R2.leg1
  GND: U1.GND, U2.VSS, U2.R_W, U2.K, R2.leg2, Part1.GND
  N6: U1.D5, Part1.CLK
  N7: U1.D6, U2.DB7
  N8: U1.D7, Part1.DIN
  N9: U1.D8, Part1.CS
  VIN: U1.Vin, Part1.VCC
  N10: U2.VO, R2.wiper

custom parts:
  NodeMCU V1.0: ESP8266 based NodeMCU
